# Fritzing sketch scheme (saved by Fritzing 0.9.10b)

parts:
  Компонент1 = Arduino Nano (Rev3.0)
  Компонент2 = LCD1602-I2C
  R1 = Resistor [tolerance=±5% resistance=100 power=0.25 package=THT]
  R3 = Resistor [tolerance=±5% resistance=10k package="0805 [SMD]"]
  M1 = DC Motor [voltage_(max)=6V voltage_(min)=3V]
  M2 = DC Motor [voltage_(max)=6V voltage_(min)=3V]
  Power_plug1 = Power plug
  R5 = Resistor [tolerance=±5% resistance=10k power=0.5W package="0603 [SMD]"]
  R4 = Resistor [tolerance=±5% power=0.25 resistance=100 package=THT]
  Q3 = Basic FET N-Channel [package="DPak [SMD]"]
  Q4 = Basic FET N-Channel [package="DPak [SMD]"]
  Encoder_round1 = Encoder round
  D1 = Rectifier Diode [part_number=1N4001 package="300 mil [THT]"]
  D2 = Rectifier Diode [part_number=1N4001 package="300 mil [THT]"]
  C1 = Ceramic Capacitor [capacitance=0.1µF voltage=35V package="100 mil [THT, multilayer]"]  # not connected
  C2 = Electrolytic Capacitor [capacitance=0.47mF voltage=6.3V package="100 mil [THT, electrolytic]"]  # not connected
  C3 = Electrolytic Capacitor [capacitance=1µF voltage=35V package="100 mil [THT, electrolytic]"]  # not connected

nets:
  GND: Компонент1.GND, Power_plug1.GND
  N1: Компонент1.D4, R4.Pin_1
  N2: Компонент1.D5, R1.Pin_1
  N3: Компонент1.A5, Компонент2.SCL
  N4: Компонент1.A4, Компонент2.SDA
  N5: Компонент1.A3, Encoder_round1.pin2
  N6: Компонент1.A2, Encoder_round1.pin3
  N7: Компонент1.A1, Encoder_round1.pin4
  N8: R1.Pin_0, R3.Pin_0, Q4.Gate
  N9: M1.pin_1, Q3.drain, D2.anode
  N10: M2.pin_1, Q4.drain, D1.anode
  N11: M2.pin_2, D1.cathode
  N12: R5.Pin_0, R4.Pin_0, Q3.Gate

notes:
  Помпы 5В
  Источник питания 5В
  Энкодер для управления дисплеем
  100Ω
  10kΩ
  s2(data)
  s1(clock)
  key(button)
  0.1uF
  470uF

custom parts:
  LCD1602-I2C: A standard character display, usually with 2x16 characters. Comes in many colors with LCM1602 IIC attached.
